# Fritzing sketch ac_control (saved by Fritzing 0.9.9b)
breadboards: 1

parts:
  WeMos_D1_Mini1 = WeMos D1 Mini
  D1 = LTE-302 [package=lte-302]
  Q1 = NPN-Transistor [part_number=2n2222 package="TO92 [THT]"]
  S1 = Pushbutton [package="[THT]"]
  R1 = Resistor [tolerance=±5% resistance=10k package="0603 [SMD]"]
  IR1 = TSOP312.., 314.. [package=THT]
  LED1 = RGB LED - (4 legs) [package="5 mm [THT]"]
  R2 = Resistor [tolerance=±5% resistance=220 package="2010 [SMD]"]
  R3 = Resistor [tolerance=±5% resistance=220 package="2010 [SMD]"]
  R4 = Resistor [tolerance=±5% resistance=220 package="2010 [SMD]"]

nets:
  N1: WeMos_D1_Mini1.5V, D1.A, S1.Pin_3, S1.Pin_4, IR1.Vs
  N2: WeMos_D1_Mini1.D0, R4.Pin_0
  N3: WeMos_D1_Mini1.D3, Q1.C
  N4: WeMos_D1_Mini1.D5, R3.Pin_0
  N5: WeMos_D1_Mini1.D6, R2.Pin_0
  N6: WeMos_D1_Mini1.D7, S1.Pin_1, S1.Pin_2, R1.Pin_0
  N7: WeMos_D1_Mini1.G, Q1.E, R1.Pin_1, IR1.Data, LED1.common_anode
  N8: D1.C, Q1.B
  N9: LED1.red_cathode, R2.Pin_1
  N10: LED1.green_cathode, R4.Pin_1
