# Fritzing sketch button_box_sketch (saved by Fritzing 0.9.9b)
perfboards: 1
stripboards: 2

parts:
  U4 = 74HC165 [part_number=SN74LS165 package="DIP16 [THT]"]
  U5 = 74HC165 [part_number=SN74LS165 package="DIP16 [THT]"]
  U6 = 74HC165 [part_number=SN74LS165 package="DIP16 [THT]"]
  U7 = 74HC165 [part_number=SN74LS165 package="DIP16 [THT]"]
  U8 = 74HC165 [part_number=SN74LS165 package="DIP16 [THT]"]
  JP2 = Header 3 [package=molex-1x3_lock]
  R25 = Resistor [tolerance=±5% resistance=10k package="2010 [SMD]"]
  R26 = Resistor [tolerance=±5% resistance=10k package="2010 [SMD]"]
  JP3 = Header 3 [package=molex-1x3_lock]
  R28 = Resistor [tolerance=±5% resistance=10k package="2010 [SMD]"]
  JP4 = Header 3 [package=molex-1x3_lock]
  R29 = Resistor [tolerance=±5% resistance=10k package="2010 [SMD]"]
  R30 = Resistor [tolerance=±5% resistance=10k package="2010 [SMD]"]
  JP5 = Header 3 [package=molex-1x3_lock]
  R31 = Resistor [tolerance=±5% resistance=10k package="2010 [SMD]"]
  R32 = Resistor [tolerance=±5% resistance=10k package="2010 [SMD]"]
  JP7 = Header 3 [package=molex-1x3_lock]
  R35 = Resistor [tolerance=±5% resistance=10k package="2010 [SMD]"]
  R36 = Resistor [tolerance=±5% resistance=10k package="2010 [SMD]"]
  JP11 = Header 3 [package=molex-1x3_lock]
  JP12 = Header 3 [package=molex-1x3_lock]
  JP13 = Header 3 [package=molex-1x3_lock]
  R43 = Resistor [tolerance=±5% resistance=10k package="2010 [SMD]"]
  R45 = Resistor [tolerance=±5% resistance=10k package="2010 [SMD]"]
  R46 = Resistor [tolerance=±5% resistance=10k package="2010 [SMD]"]
  R47 = Resistor [tolerance=±5% resistance=10k package="2010 [SMD]"]
  R48 = Resistor [tolerance=±5% resistance=10k package="2010 [SMD]"]
  JP14 = Header 3 [package=molex-1x3_lock]
  JP15 = Header 3 [package=molex-1x3_lock]
  R49 = Resistor [tolerance=±5% resistance=10k package="2010 [SMD]"]
  R51 = Resistor [tolerance=±5% resistance=10k package="2010 [SMD]"]
  R52 = Resistor [tolerance=±5% resistance=10k package="2010 [SMD]"]
  R53 = Resistor [tolerance=±5% resistance=10k package="2010 [SMD]"]
  JP17 = Header 3 [package=molex-1x3_lock]
  JP18 = Header 3 [package=molex-1x3_lock]
  JP19 = Header 3 [package=molex-1x3_lock]
  R55 = Resistor [tolerance=±5% resistance=10k package="2010 [SMD]"]
  R57 = Resistor [tolerance=±5% resistance=10k package="2010 [SMD]"]
  R58 = Resistor [tolerance=±5% resistance=10k package="2010 [SMD]"]
  R59 = Resistor [tolerance=±5% resistance=10k package="2010 [SMD]"]
  R60 = Resistor [tolerance=±5% resistance=10k package="2010 [SMD]"]
  JP20 = Header 3 [package=molex-1x3_lock]
  R62 = Resistor [tolerance=±5% resistance=10k package="2010 [SMD]"]
  R63 = Resistor [tolerance=±5% resistance=10k package="2010 [SMD]"]
  R64 = Resistor [tolerance=±5% resistance=10k package="2010 [SMD]"]
  R66 = Resistor [tolerance=±5% resistance=10k package="2010 [SMD]"]
  J1 = male pin header, 4 pins [form="♂ (male)"]
  J2 = male pin header, 4 pins [form="♂ (male)"]
  J3 = male pin header, 4 pins [form="♂ (male)"]
  J4 = male pin header, 4 pins [form="♂ (male)"]
  J5 = male pin header, 4 pins [form="♂ (male)"]
  R67 = Resistor [tolerance=±5% resistance=270 package="0805 [SMD]"]
  R68 = Resistor [tolerance=±5% resistance=270 package="0805 [SMD]"]
  R69 = Resistor [tolerance=±5% resistance=270 package="0805 [SMD]"]
  R70 = Resistor [tolerance=±5% resistance=270 package="0805 [SMD]"]
  R71 = Resistor [tolerance=±5% resistance=270 package="0805 [SMD]"]
  R72 = Resistor [tolerance=±5% resistance=10k package="2010 [SMD]"]
  R73 = Resistor [tolerance=±5% resistance=10k package="2010 [SMD]"]
  R75 = Resistor [tolerance=±5% resistance=10k package="2010 [SMD]"]
  R76 = Resistor [tolerance=±5% resistance=10k package="2010 [SMD]"]
  R56 = Resistor [tolerance=±5% resistance=10k package="2010 [SMD]"]
  R27 = Resistor [tolerance=±5% resistance=10k package="2010 [SMD]"]
  R44 = Resistor [tolerance=±5% resistance=10k package="2010 [SMD]"]
  JP21 = Header 3 [package=molex-1x3_lock]
  J7 = male pin header, 4 pins [form="♂ (male)"]
  R79 = Resistor [tolerance=±5% resistance=10k package="2010 [SMD]"]
  R80 = Resistor [tolerance=±5% resistance=10k package="2010 [SMD]"]
  R81 = Resistor [tolerance=±5% resistance=10k package="2010 [SMD]"]
  R82 = Resistor [tolerance=±5% resistance=10k package="2010 [SMD]"]
  R83 = Resistor [tolerance=±5% resistance=10k package="2010 [SMD]"]
  C1 = Electrolytic Capacitor [capacitance=1mF voltage=35V package="0605 [SMD, electrolytic]"]
  C2 = Electrolytic Capacitor [capacitance=1mF voltage=35V package="0605 [SMD, electrolytic]"]
  C3 = Electrolytic Capacitor [capacitance=1mF voltage=35V package="0605 [SMD, electrolytic]"]
  C4 = Electrolytic Capacitor [capacitance=1mF voltage=35V package="0605 [SMD, electrolytic]"]
  C5 = Electrolytic Capacitor [capacitance=1mF voltage=35V package="0605 [SMD, electrolytic]"]
  R74 = Resistor [tolerance=±5% resistance=10k package="2010 [SMD]"]
  J8 = male pin header, 2 pins [form="♂ (male)"]

nets:
  N1: U4.Q1, U5.Q1, U6.Q1, U7.Q1, U8.Q1, J7.pin3
  N2: U4.Q2, U5.Q2, U6.Q2, U7.Q2, U8.Q2, J7.pin4
  N3: U4.Q3, R80.Pin_1
  N4: U4.Q4, R79.Pin_1
  N5: U4.Q5, J4.pin1, R76.Pin_1
  N6: U4.Q6, J3.pin1, R75.Pin_1
  GND: U4.GND, U5.GND, U6.GND, U7.GND, U8.GND, R25.Pin_0, R26.Pin_0, R28.Pin_0, R29.Pin_0, R30.Pin_0, R31.Pin_0, R32.Pin_0, R35.Pin_0, R36.Pin_0, R43.Pin_0, R45.Pin_0, R46.Pin_0, R47.Pin_0, R48.Pin_0, R49.Pin_0, R51.Pin_0, R52.Pin_0, R53.Pin_0, R55.Pin_0, R57.Pin_0, R58.Pin_0, R59.Pin_0, R60.Pin_0, R62.Pin_0, R63.Pin_0, R64.Pin_0, R66.Pin_0, J1.pin1, J3.pin4, J4.pin4, J5.pin1, R72.Pin_0, R73.Pin_0, R75.Pin_0, R76.Pin_0, R56.Pin_0, R27.Pin_0, R44.Pin_0, R79.Pin_0, R80.Pin_0, R81.Pin_0, R82.Pin_0, R83.Pin_0, C1.-, C2.-, C3.-, C4.-, C5.-, R74.Pin_0, J8.pin2
  N7: U4.Q7', J7.pin1
  N8: U4.MR, U5.Q7'
  N9: U4.SH_CP, J5.pin4, R74.Pin_1
  N10: U4.ST_CP, R81.Pin_1
  N11: U4.OE, R82.Pin_1
  N12: U4.DS, R83.Pin_1
  N13: U4.Q0, U5.Q0, U6.Q0, U7.Q0, U8.Q0, J7.pin2
  VCC: U4.VCC, U5.VCC, U6.VCC, U7.VCC, U8.VCC, JP2.3, JP3.3, JP4.3, JP5.3, JP7.3, JP11.3, JP12.3, JP13.3, JP14.3, JP15.3, JP17.3, JP18.3, JP19.3, JP20.3, J1.pin2, J2.pin2, J3.pin3, J4.pin3, J5.pin2, R67.Pin_0, R68.Pin_0, R69.Pin_0, R70.Pin_0, R71.Pin_0, JP21.3, C1.+, C2.+, C3.+, C4.+, C5.+, J8.pin1
  N14: U5.Q3, JP20.1, R62.Pin_1
  N15: U5.Q4, JP20.2, R64.Pin_1
  N16: U5.Q5, R66.Pin_1, JP21.1
  N17: U5.Q6, R63.Pin_1, JP21.2
  N18: U5.MR, U6.Q7'
  N19: U5.SH_CP, JP15.1, R49.Pin_1
  N20: U5.ST_CP, JP15.2, R51.Pin_1
  N21: U5.OE, J1.pin4, R72.Pin_1
  N22: U5.DS, J2.pin4, R73.Pin_1
  N23: U6.Q3, JP17.1, R59.Pin_1
  N24: U6.Q4, JP17.2, R58.Pin_1
  N25: U6.Q5, JP18.1, R55.Pin_1
  N26: U6.Q6, JP18.2, R57.Pin_1
  N27: U6.MR, U7.Q7'
  N28: U6.SH_CP, JP13.1, R48.Pin_1
  N29: U6.ST_CP, JP13.2, R44.Pin_1
  N30: U6.OE, JP14.1, R53.Pin_1
  N31: U6.DS, JP14.2, R52.Pin_1
  N32: U7.Q3, JP19.1, R60.Pin_1
  N33: U7.Q4, JP19.2, R56.Pin_1
  N34: U7.Q5, JP7.1, R36.Pin_1
  N35: U7.Q6, JP7.2, R35.Pin_1
  N36: U7.MR, U8.Q7'
  N37: U7.SH_CP, JP11.1, R47.Pin_1
  N38: U7.ST_CP, JP11.2, R46.Pin_1
  N39: U7.OE, JP12.1, R43.Pin_1
  N40: U7.DS, JP12.2, R45.Pin_1
  N41: U8.Q3, JP2.1, R25.Pin_1
  N42: U8.Q4, JP2.2, R26.Pin_1
  N43: U8.Q5, JP5.1, R32.Pin_1
  N44: U8.Q6, JP5.2, R31.Pin_1
  N45: U8.SH_CP, JP4.1, R30.Pin_1
  N46: U8.ST_CP, JP4.2, R29.Pin_1
  N47: U8.OE, JP3.1, R28.Pin_1
  N48: U8.DS, JP3.2, R27.Pin_1
  N49: J1.pin3, R69.Pin_1
  N50: J2.pin3, R70.Pin_1
  N51: J3.pin2, R67.Pin_1
  N52: J4.pin2, R68.Pin_1
  N53: J5.pin3, R71.Pin_1

notes:
  resistor from red is for led

custom parts:
  74HC165: 8-bit parallel-load shift registers
