# Fritzing sketch button_box_sketch_small_v3 (saved by Fritzing 0.9.9b)
circuit board: 4.40879cm x 3.46583cm
stripboards: 2
perfboards: 1

parts:
  J_POWER = male pin header, 2 pins [form="♂ (male)"]
  J4 = male pin header, 4 pins [form="♂ (male)"]
  J2 = male pin header, 4 pins [form="♂ (male)"]
  J_DATA = male pin header, 4 pins [form="♂ (male)"]
  R_10k = Resistor [tolerance=±5% resistance=10k power=0.25 package=THT]
  R_10k_2 = Resistor [tolerance=±5% resistance=10k power=0.25 package=THT]
  R_10k_3 = Resistor [tolerance=±5% resistance=10k power=0.25 package=THT]
  R_10k_4 = Resistor [tolerance=±5% resistance=10k power=0.25 package=THT]
  R_270 = Resistor [tolerance=±5% resistance=270 power=0.25 package=THT]
  R_270_2 = Resistor [tolerance=±5% resistance=270 power=0.25 package=THT]
  J3 = male pin header, 4 pins [form="♂ (male)"]
  J1 = male pin header, 4 pins [form="♂ (male)"]
  R_270_3 = Resistor [tolerance=±5% power=0.25 resistance=270 package=THT]
  R_270_4 = Resistor [tolerance=±5% resistance=270 power=0.25 package=THT]

nets:
  N1: J_POWER.pin1, J4.pin2, J2.pin3, R_270.Pin_0, R_270_2.Pin_0, J3.pin2, J1.pin3, R_270_3.Pin_0, R_270_4.Pin_0
  N2: J_POWER.pin2, J4.pin1, J2.pin4, R_10k.Pin_0, R_10k_2.Pin_0, R_10k_3.Pin_0, R_10k_4.Pin_0, J3.pin1, J1.pin4
  N3: J4.pin3, R_270_2.Pin_1
  N4: J4.pin4, J_DATA.pin3, R_10k_4.Pin_1
  N5: J2.pin1, J_DATA.pin2, R_10k.Pin_1
  N6: J2.pin2, R_270.Pin_1
  N7: J_DATA.pin1, R_10k_2.Pin_1, J1.pin1
  N8: J_DATA.pin4, R_10k_3.Pin_1, J3.pin4
  N9: J3.pin3, R_270_3.Pin_1
  N10: J1.pin2, R_270_4.Pin_1
